# Fritzing sketch aquarium-electrical-circuit (saved by Fritzing 0.9.3b)
breadboards: 1

parts:
  U1 = NodeMCU V3.0
  U2 = 4-Channel 5v Relay Shield [package=relay-4ch5v10a]
  DS3 = DS18B20 1-Wire Temperature Sensor [part_number=DS18B20]
  R2 = Resistor [tolerance=±5% resistance=4.7k package=THT]
  S7 = Pushbutton [package="[SMD]"]
  S8 = Pushbutton [package="[SMD]"]
  S9 = Pushbutton [package="[SMD]"]
  S10 = Pushbutton [package="[SMD]"]
  R4 = Resistor [tolerance=±5% resistance=10k package=THT]
  R5 = Resistor [tolerance=±5% resistance=10k package=THT]
  R6 = Resistor [tolerance=±5% resistance=10k package=THT]
  R7 = Resistor [tolerance=±5% resistance=10k package=THT]
  JACK2 = 2.1mm Barrel Jack with Terminal Block
  JP11 = Header 3 [package=screwterminal-3.5mm-3_lock.007s]  # not connected

nets:
  N1: U1.D0, U2.IN1
  N2: U1.D1, U2.IN2
  N3: U1.D2, U2.IN3
  N4: U1.D3, U2.IN4
  N5: U1.D4, DS3.DQ, R2.Pin_1
  3V3: U1.3V3, DS3.VDD, R2.Pin_0, S7.Pin_3, S7.Pin_4, S8.Pin_3, S8.Pin_4, S9.Pin_3, S9.Pin_4, S10.Pin_3, S10.Pin_4
  GND: U1.GND#6, U1.GND#13, U1.GND#16, U1.GND#33, U2.GND, DS3.GND, R4.Pin_1, R5.Pin_1, R6.Pin_1, R7.Pin_1, JACK2.NEG
  N6: U1.D5, S7.Pin_1, S7.Pin_2, R4.Pin_0
  N7: U1.D6, S8.Pin_1, S8.Pin_2, R5.Pin_0
  N8: U1.D7, S9.Pin_1, S9.Pin_2, R6.Pin_0
  N9: U1.D8, S10.Pin_1, S10.Pin_2, R7.Pin_0
  VIN: U1.Vin, U2.VCC, JACK2.POS

notes:
  Manual control switches
  DS18B20 Waterproof
  temp sensor
  Control unit
  5V DC
  power
  supply
  Outlet 4
  Heater
  Outlet 3
  Water Filter
  Outlet 2
  Lighting
  Outlet 1
  Air Pump
  240V AC
  power
  supply
  Relay shield
  Fish tank control wiring circuit

custom parts:
  NodeMCU V3.0: ESP8266 based NodeMCU
  4-Channel 5v Relay Shield: 4 Channel 5v Relay Shield w. 2x SPD-06VDC-SD-C
